# Fritzing sketch layout (saved by Fritzing 0.9.4)
circuit board: 4.08658cm x 3.57481cm
breadboards: 1

parts:
  WeMos_D1_Mini1 = WeMos D1 Mini
  LED1 = RGB LED - (4 legs) [package="5 mm [THT]"]
  R3 = Resistor [tolerance=±5% resistance=220 package="1206 [SMD]"]
  R2 = Resistor [tolerance=±5% resistance=220 package="1206 [SMD]"]
  R1 = Resistor [tolerance=±5% resistance=220 package="1206 [SMD]"]

nets:
  N1: WeMos_D1_Mini1.5V, LED1.common_anode
  N2: WeMos_D1_Mini1.D2, R1.Pin_0
  N3: WeMos_D1_Mini1.D3, R2.Pin_0
  N4: WeMos_D1_Mini1.D4, R3.Pin_0
  N5: LED1.red_cathode, R1.Pin_1
  N6: LED1.green_cathode, R2.Pin_1
  N7: LED1.blue_cathode, R3.Pin_1
